// Logisim project qn1.circ as structural Verilog: 1 circuit, main circuit Priority encoder
module Priority_encoder (
  input  A0,
  input  A1,
  input  A2,
  input  A3,
  input  A4,
  input  A5,
  input  A6,
  input  A7,
  output F0,
  output F1,
  output F2
);

  Priority_Encoder priority_encoder_1 (
    .in0(A0), .in1(A1), .in2(A2), .in3(A3), .in4(A4), .in5(A5), .in6(A6), .in7(A7), .out({F2, F1, F0}));  // open: en_in, gs, en_out
endmodule
