// Logisim project qn2.circ as structural Verilog: 1 circuit, main circuit sequential circuit
module sequential_circuit (
  input  x,
  output z
);

  wire and_2_out, clock_1_out, j_k_ff_1_q, j_k_ff_1_qn, j_k_ff_2_q, j_k_ff_3_qn, not_1_out, or_1_out;

  and and_1 (z, x, j_k_ff_2_q, j_k_ff_1_q);
  and and_2 (and_2_out, x, j_k_ff_2_q, j_k_ff_3_qn);
  Clock clock_1 (.out(clock_1_out));
  not not_1 (not_1_out, x);
  J_K_Flip_Flop #(.trigger("falling")) j_k_ff_1 (
    .J(and_2_out), .clk(clock_1_out), .K(not_1_out), .Q(j_k_ff_1_q), .Qn(j_k_ff_1_qn));  // open: preset, en, reset
  J_K_Flip_Flop #(.trigger("falling")) j_k_ff_2 (
    .J(x), .clk(clock_1_out), .K(or_1_out), .Q(j_k_ff_2_q));  // open: Qn, preset, en, reset
  J_K_Flip_Flop #(.trigger("falling")) j_k_ff_3 (
    .J(1'b1), .clk(clock_1_out), .K(1'b1), .Qn(j_k_ff_3_qn));  // open: Q, preset, en, reset
  or or_1 (or_1_out, not_1_out, j_k_ff_1_qn);
endmodule
