// Logisim project circuits.circ as structural Verilog: 10 circuits, main circuit JK with preset
module Half_Adder (
  input  X,
  input  Y,
  output S,
  output C
);

  wire not_1_out, not_2_out, or_1_out, or_2_out;

  not not_1 (not_1_out, X);
  not not_2 (not_2_out, Y);
  or or_1 (or_1_out, X, Y);
  or or_2 (or_2_out, not_1_out, not_2_out);
  and and_1 (S, or_1_out, or_2_out);
  not not_3 (C, or_2_out);
endmodule

module Half_Adder_XOR (
  input  X,
  input  Y,
  output S,
  output C
);

  xor xor_1 (S, X, Y);
  and and_1 (C, X, Y);
endmodule

module Full_Adder (
  input  X,
  input  Y,
  input  Z,
  output S,
  output C
);

  wire and_1_out, and_2_out, xor_1_out;

  xor xor_1 (xor_1_out, X, Y);
  and and_1 (and_1_out, X, Y);
  xor xor_2 (S, xor_1_out, Z);
  and and_2 (and_2_out, xor_1_out, Z);
  or or_1 (C, and_2_out, and_1_out);
endmodule

module Full_Adder_w_block (
  input  X,
  input  Y,
  input  Z,
  output S,
  output C
);

  wire half_adder_1_c, half_adder_1_s, half_adder_xor_1_c;

  Half_Adder half_adder_1 (.X(X), .Y(Y), .S(half_adder_1_s), .C(half_adder_1_c));
  Half_Adder_XOR half_adder_xor_1 (.X(half_adder_1_s), .Y(Z), .S(S), .C(half_adder_xor_1_c));
  or or_1 (C, half_adder_xor_1_c, half_adder_1_c);
endmodule

module _4_bit_parallel_adder (
  input  [3:0] X,
  input  [3:0] Y,
  input  Cin,
  output [3:0] S,
  output Cout
);

  wire full_adder_1_c, full_adder_2_c, full_adder_3_c;

  Full_Adder full_adder_1 (.X(X[0]), .Y(Y[0]), .Z(Cin), .S(S[0]), .C(full_adder_1_c));
  Full_Adder full_adder_2 (.X(X[1]), .Y(Y[1]), .Z(full_adder_1_c), .S(S[1]), .C(full_adder_2_c));
  Full_Adder full_adder_3 (.X(X[2]), .Y(Y[2]), .Z(full_adder_2_c), .S(S[2]), .C(full_adder_3_c));
  Full_Adder full_adder_4 (.X(X[3]), .Y(Y[3]), .Z(full_adder_3_c), .S(S[3]), .C(Cout));
endmodule

module _16_bit_adder (
  input  [15:0] X,
  input  [15:0] Y,
  input  Cin,
  output [15:0] _16_Bits,
  output Bit_17
);

  wire n4_bit_parallel_adder_1_cout, n4_bit_parallel_adder_2_cout, n4_bit_parallel_adder_3_cout;

  _4_bit_parallel_adder u_4_bit_parallel_adder_1 (
    .X(X[3:0]), .Y(Y[3:0]), .Cin(Cin), .S(_16_Bits[3:0]), .Cout(n4_bit_parallel_adder_1_cout));
  _4_bit_parallel_adder u_4_bit_parallel_adder_2 (
    .X(X[7:4]), .Y(Y[7:4]), .Cin(n4_bit_parallel_adder_1_cout), .S(_16_Bits[7:4]),
    .Cout(n4_bit_parallel_adder_2_cout));
  _4_bit_parallel_adder u_4_bit_parallel_adder_3 (
    .X(X[11:8]), .Y(Y[11:8]), .Cin(n4_bit_parallel_adder_2_cout), .S(_16_Bits[11:8]),
    .Cout(n4_bit_parallel_adder_3_cout));
  _4_bit_parallel_adder u_4_bit_parallel_adder_4 (
    .X(X[15:12]), .Y(Y[15:12]), .Cin(n4_bit_parallel_adder_3_cout), .S(_16_Bits[15:12]), .Cout(Bit_17));
endmodule

module Priority_encoder (
  input  A0,
  input  A1,
  input  A2,
  input  A3,
  input  A4,
  input  A5,
  input  A6,
  input  A7,
  output F0,
  output F1,
  output F2
);

  Priority_Encoder priority_encoder_1 (
    .in0(A0), .in1(A1), .in2(A2), .in3(A3), .in4(A4), .in5(A5), .in6(A6), .in7(A7), .out({F2, F1, F0}));  // open: en_in, gs, en_out
endmodule

module JK_with_preset (
  input  Clear,
  input  Preset,
  output A,
  output B
);

  wire and_1_out, clock_1_out, not_1_out;

  Clock clock_1 (.out(clock_1_out));
  and and_1 (and_1_out, A, B);
  J_K_Flip_Flop j_k_ff_1 (
    .J(1'b1), .clk(clock_1_out), .K(and_1_out), .Q(A), .preset(Preset), .en(1'b1), .reset(Clear));  // open: Qn
  not not_1 (not_1_out, and_1_out);
  J_K_Flip_Flop j_k_ff_2 (
    .J(1'b0), .clk(clock_1_out), .K(not_1_out), .Q(B), .preset(Preset), .en(1'b1), .reset(Clear));  // open: Qn
endmodule

module sequential_circuit (
  input  x,
  output z
);

  wire and_2_out, clock_1_out, j_k_ff_1_q, j_k_ff_1_qn, j_k_ff_2_q, j_k_ff_3_qn, not_1_out, or_1_out;

  and and_1 (z, x, j_k_ff_2_q, j_k_ff_1_q);
  and and_2 (and_2_out, x, j_k_ff_2_q, j_k_ff_3_qn);
  not not_1 (not_1_out, x);
  J_K_Flip_Flop #(.trigger("falling")) j_k_ff_1 (
    .J(and_2_out), .clk(clock_1_out), .K(not_1_out), .Q(j_k_ff_1_q), .Qn(j_k_ff_1_qn));  // open: preset, en, reset
  J_K_Flip_Flop #(.trigger("falling")) j_k_ff_2 (
    .J(x), .clk(clock_1_out), .K(or_1_out), .Q(j_k_ff_2_q));  // open: Qn, preset, en, reset
  J_K_Flip_Flop #(.trigger("falling")) j_k_ff_3 (
    .J(1'b1), .clk(clock_1_out), .K(1'b1), .Qn(j_k_ff_3_qn));  // open: Q, preset, en, reset
  Clock clock_1 (.out(clock_1_out));
  or or_1 (or_1_out, not_1_out, j_k_ff_1_qn);
endmodule

module Magnitude_Comparator (
  input  [3:0] X,
  input  [3:0] Y
);

  wire and_1_out, and_2_out, and_3_out, and_4_out, or_1_out, or_2_out;

  and and_1 (and_1_out, ~X[0], Y[0]);  // AND_Gate
  and and_2 (and_2_out, ~X[0], Y[0]);  // AND_Gate
  and and_3 (and_3_out, ~X[1], Y[1]);  // AND_Gate
  and and_4 (and_4_out, ~X[1], Y[1]);  // AND_Gate
  or or_1 (or_1_out, and_1_out, and_2_out);
  or or_2 (or_2_out, and_3_out, and_4_out);
  // OR_Gate or_3 has open pins: in0=and_1_out, out=open
endmodule
